# Fritzing sketch keypad (saved by Fritzing 0.9.3b)
breadboards: 1

parts:
  Part1 = Arduino Uno (Rev3)
  Part2 = sx1509 breakout
  Part3 = Thumb Joystick  # not connected

nets:
  N1: Part1.D8, Part1.D9_PWM, Part1.D2, Part1.D3_PWM, Part1.D4, Part1.D5_PWM, Part1.D6_PWM, Part1.D7, Part2.PWRBUSA

notes:
  this is a keypad
  (left to right on keypad: 5 4 3 2 9 8 7 6)
  need to install Keypad by ark library
