# Fritzing sketch laser with photocell and button (saved by Fritzing 0.8.7b)
breadboards: 1

parts:
  Part1 = Arduino Uno (Rev3)
  R1 = Photocell (LDR) [package=THT]
  S1 = Pushbutton [package="[THT]"]
  Laser_Emitor = Ambient Light Sensor (TEMT6000 Breakout Board)
  Electromagnet_sensor = Ambient Light Sensor (TEMT6000 Breakout Board)
  R2 = Resistor [tolerance=±5% resistance=10k package=THT]
  Part4 = Thumb Joystick
  Sound_Sensor = Ambient Light Sensor (TEMT6000 Breakout Board)
  Flame_Sensor = Ambient Light Sensor (TEMT6000 Breakout Board)
  Water_sensor = Ambient Light Sensor (TEMT6000 Breakout Board)
  Part8 = Arduino Uno (Rev3)
  Keypad = Triple Axis Accelerometer Breakout - ADXL345
  R3 = Resistor [tolerance=±5% resistance=10k package=THT]

nets:
  N1: Part1.A0, Part4.HORZ
  N2: Part1.A1, Part4.VERT
  N3: Part1.A2, Sound_Sensor.S
  N4: Part1.A3, Flame_Sensor.S
  N5: Part1.A4/SDA, Water_sensor.S
  N6: Part1.A5/SCL, R1.pin_1, R2.Pin_0
  N7: Part1.D10_PWM/SS, Part4.SEL
  N8: Part1.D11_PWM/MOSI, Electromagnet_sensor.S
  N9: Part1.D12/MISO, S1.Pin_1, S1.Pin_2, R3.Pin_0
  N10: Part1.D13/SCK, Laser_Emitor.S
  N11: Part1.D2, Part8.D1/TX
  N12: Part1.D3_PWM, Part8.D0/RX
  VCC: Part1.5V, S1.Pin_3, S1.Pin_4, Laser_Emitor.VCC, Electromagnet_sensor.VCC, R2.Pin_1, Part4.VCC, Sound_Sensor.VCC, Flame_Sensor.VCC, Water_sensor.VCC
  GND: Part1.GND, R1.pin_0, Laser_Emitor.GND, Electromagnet_sensor.GND, Part4.GND, Sound_Sensor.GND, Flame_Sensor.GND, Water_sensor.GND, R3.Pin_1
  N13: Part8.D8, Keypad.SDO
  N14: Part8.D9_PWM, Keypad.INT2
  N15: Part8.D2, Keypad.INT1
  N16: Part8.D3_PWM, Keypad.CS
  N17: Part8.D4, Keypad.VCC
  N18: Part8.D5_PWM, Keypad.GND
  N19: Part8.D6_PWM, Keypad.SCL
  N20: Part8.D7, Keypad.SDA

notes:
  This is a laser
  This is a electromagnetic sensor
  This is a sound sensor
  This is a flame sensor
  this is a keypad
  (left to right on keypad: 5 4 3 2 9 8 7 6
  This is a water sensor
